// Logisim project Ex1.circ as structural Verilog: 1 circuit, main circuit main
module main (
  input  A,
  input  [3:0] A_2,
  input  B,
  input  [3:0] B_2,
  output C,
  output [3:0] C_2,
  output D,
  output [3:0] D_2,
  output E,
  output [3:0] E_2,
  output F,
  output [3:0] F_2,
  output G,
  output [3:0] G_2
);

  not not_1 (C, A);
  and and_1 (D, A, B);
  or or_1 (E, A, B);
  nand nand_1 (F, A, B);
  xor xor_1 (G, A, B);
  assign C_2 = ~A_2;  // NOT_Gate not_2, 4 bits wide
  assign D_2 = A_2 & B_2;  // AND_Gate and_2, 4 bits wide
  assign E_2 = A_2 | B_2;  // OR_Gate or_2, 4 bits wide
  assign F_2 = ~(A_2 & B_2);  // NAND_Gate nand_2, 4 bits wide
  assign G_2 = A_2 ^ B_2;  // XOR_Gate xor_2, 4 bits wide
endmodule
