// Logisim project Ex2.circ as structural Verilog: 1 circuit, main circuit main
module main (
  input  X,
  input  Y,
  input  A,
  input  B,
  input  [7:0] X_2,
  input  [7:0] Y_2,
  input  [7:0] A_2,
  input  [7:0] B_2,
  output C,
  output [7:0] C_2
);

  wire and_1_out, and_2_out, and_3_out, and_4_out, not_1_out, not_2_out, not_3_out, not_4_out, not_5_out;
  wire [7:0] and_5_out, and_6_out, and_7_out, and_8_out, not_6_out, not_7_out, not_8_out, not_9_out,
       not_10_out, or_2_out;

  not not_1 (not_1_out, Y);
  and and_1 (and_1_out, not_1_out, A, B);
  not not_2 (not_2_out, A);
  and and_2 (and_2_out, Y, not_2_out, not_3_out);
  not not_3 (not_3_out, B);
  not not_4 (not_4_out, A);
  and and_3 (and_3_out, X, not_4_out, B);
  and and_4 (and_4_out, X, A, not_5_out);
  not not_5 (not_5_out, B);
  or or_1 (C, and_1_out, and_2_out, and_3_out, and_4_out);
  assign not_6_out = ~Y_2;  // NOT_Gate not_6, 8 bits wide
  assign not_7_out = ~A_2;  // NOT_Gate not_7, 8 bits wide
  assign not_8_out = ~B_2;  // NOT_Gate not_8, 8 bits wide
  assign not_9_out = ~A_2;  // NOT_Gate not_9, 8 bits wide
  assign not_10_out = ~B_2;  // NOT_Gate not_10, 8 bits wide
  assign and_5_out = not_6_out & A_2 & B_2;  // AND_Gate and_5, 8 bits wide
  assign and_6_out = Y_2 & not_7_out & not_8_out;  // AND_Gate and_6, 8 bits wide
  assign and_7_out = X_2 & not_9_out & B_2;  // AND_Gate and_7, 8 bits wide
  assign and_8_out = X_2 & A_2 & not_10_out;  // AND_Gate and_8, 8 bits wide
  assign or_2_out = and_5_out | and_6_out | and_7_out | and_8_out;  // OR_Gate or_2, 8 bits wide
endmodule
