// Logisim project Ex3.circ as structural Verilog: 1 circuit, main circuit main
module main (
  input  A,
  input  B,
  input  C,
  output O_P
);

  wire and_1_out, and_2_out, and_3_out;

  and and_1 (and_1_out, A, A, B);
  and and_2 (and_2_out, B, C);
  and and_3 (and_3_out, C, A);
  or or_1 (O_P, and_1_out, and_2_out, and_3_out);
endmodule
