// Logisim project Ex4.circ as structural Verilog: 1 circuit, main circuit main
module main (
  input  in_1,
  input  in_2,
  input  in_3,
  input  in_4,
  output O1,
  output O2,
  output O3
);

  wire and_1_out, and_2_out, and_3_out, and_4_out, and_5_out, and_6_out, and_7_out, not_1_out, not_2_out,
       not_3_out, not_4_out, not_5_out, not_6_out;

  Hex_Digit_Display hex_digit_display_1 (.value({1'b0, in_3, in_2, in_1}));  // open: dp
  and and_1 (and_1_out, in_2, in_3);
  and and_2 (and_2_out, in_1, in_3);
  and and_3 (and_3_out, in_1, in_2);
  not not_1 (not_1_out, in_1);
  not not_2 (not_2_out, in_2);
  not not_3 (not_3_out, in_1);
  not not_4 (not_4_out, in_3);
  not not_5 (not_5_out, in_2);
  not not_6 (not_6_out, in_3);
  not not_7 (O3, in_3);
  or or_1 (O1, and_1_out, and_2_out, and_3_out);
  and and_4 (and_4_out, not_1_out, not_2_out, in_3);
  and and_5 (and_5_out, not_3_out, in_2, not_4_out);
  and and_6 (and_6_out, in_1, not_5_out, not_6_out);
  and and_7 (and_7_out, in_1, in_2, in_3);
  or or_2 (O2, and_4_out, and_5_out, and_6_out, and_7_out);
  Hex_Digit_Display hex_digit_display_2 (.value({O1, O2, O3, in_4}));  // open: dp

  // Notes on the sheet:
  //   Manan Jain (211B173)
endmodule
