// Logisim project Exp2.circ as structural Verilog: 7 circuits, main circuit main
module main (
  input  [3:0] A,
  input  [3:0] B
);

  wire fa_2_carry, fa_3_carry, ha_1_carry;
  wire [0:0] fa_1_carry;
  wire [3:0] ha_1_sum;

  Hex_Digit_Display hex_digit_display_1 (.value({3'b000, fa_1_carry[0]}));  // open: dp
  FA fa_1 (.A(A[3]), .B(B[3]), .C(fa_2_carry), .SUM(ha_1_sum[3]), .CARRY(fa_1_carry[0]));
  Hex_Digit_Display hex_digit_display_2 (.value(A));  // open: dp
  FA fa_2 (.A(A[2]), .B(B[2]), .C(fa_3_carry), .SUM(ha_1_sum[2]), .CARRY(fa_2_carry));
  FA fa_3 (.A(A[1]), .B(B[1]), .C(ha_1_carry), .SUM(ha_1_sum[1]), .CARRY(fa_3_carry));
  Hex_Digit_Display hex_digit_display_3 (.value(B));  // open: dp
  HA ha_1 (.A(A[0]), .B(B[0]), .SUM(ha_1_sum[0]), .CARRY(ha_1_carry));
  Hex_Digit_Display hex_digit_display_4 (.value(ha_1_sum));  // open: dp

  // Notes on the sheet:
  //   CARRY_OUT
  //   SUM
endmodule

module HA (
  input  A,
  input  B,
  output SUM,
  output CARRY
);

  xor xor_1 (SUM, A, B);
  and and_1 (CARRY, A, B);
endmodule

module HS (
  input  A,
  input  B,
  output DIFF,
  output BORROW
);

  wire not_1_out;

  not not_1 (not_1_out, B);
  xor xor_1 (DIFF, A, B);
  and and_1 (BORROW, A, not_1_out);
endmodule

module FAgates (
  input  A,
  input  B,
  input  C,
  output SUM,
  output CARRY
);

  wire and_1_out, and_2_out, xor_1_out;

  xor xor_1 (xor_1_out, A, B);
  xor xor_2 (SUM, xor_1_out, C);
  and and_1 (and_1_out, C, xor_1_out);
  and and_2 (and_2_out, A, B);
  or or_1 (CARRY, and_1_out, and_2_out);
endmodule

module FA (
  input  A,
  input  B,
  input  C,
  output SUM,
  output CARRY
);

  wire ha_1_carry, ha_1_sum, ha_2_carry;

  HA ha_1 (.A(B), .B(C), .SUM(ha_1_sum), .CARRY(ha_1_carry));
  HA ha_2 (.A(A), .B(ha_1_sum), .SUM(SUM), .CARRY(ha_2_carry));
  or or_1 (CARRY, ha_2_carry, ha_1_carry);
endmodule

module _4BitAdder (
  input  [3:0] A,
  input  [3:0] B
);

  wire fa_2_carry, fa_3_carry, ha_1_carry;
  wire [0:0] fa_1_carry;
  wire [3:0] ha_1_sum;

  Hex_Digit_Display hex_digit_display_1 (.value({3'b000, fa_1_carry[0]}));  // open: dp
  FA fa_1 (.A(A[3]), .B(B[3]), .C(fa_2_carry), .SUM(ha_1_sum[3]), .CARRY(fa_1_carry[0]));
  Hex_Digit_Display hex_digit_display_2 (.value(A));  // open: dp
  FA fa_2 (.A(A[2]), .B(B[2]), .C(fa_3_carry), .SUM(ha_1_sum[2]), .CARRY(fa_2_carry));
  FA fa_3 (.A(A[1]), .B(B[1]), .C(ha_1_carry), .SUM(ha_1_sum[1]), .CARRY(fa_3_carry));
  Hex_Digit_Display hex_digit_display_3 (.value(B));  // open: dp
  HA ha_1 (.A(A[0]), .B(B[0]), .SUM(ha_1_sum[0]), .CARRY(ha_1_carry));
  Hex_Digit_Display hex_digit_display_4 (.value(ha_1_sum));  // open: dp

  // Notes on the sheet:
  //   CARRY_OUT
  //   SUM
endmodule

module AdderSubtractor (
  input  [3:0] A,
  input  [3:0] B
);

  wire fa_2_carry, fa_3_carry, ha_1_carry;
  wire [0:0] fa_1_carry;
  wire [3:0] ha_1_sum;

  Hex_Digit_Display hex_digit_display_1 (.value({3'b000, fa_1_carry[0]}));  // open: dp
  FA fa_1 (.A(A[3]), .B(B[3]), .C(fa_2_carry), .SUM(ha_1_sum[3]), .CARRY(fa_1_carry[0]));
  Hex_Digit_Display hex_digit_display_2 (.value(A));  // open: dp
  FA fa_2 (.A(A[2]), .B(B[2]), .C(fa_3_carry), .SUM(ha_1_sum[2]), .CARRY(fa_2_carry));
  FA fa_3 (.A(A[1]), .B(B[1]), .C(ha_1_carry), .SUM(ha_1_sum[1]), .CARRY(fa_3_carry));
  Hex_Digit_Display hex_digit_display_3 (.value(B));  // open: dp
  HA ha_1 (.A(A[0]), .B(B[0]), .SUM(ha_1_sum[0]), .CARRY(ha_1_carry));
  Hex_Digit_Display hex_digit_display_4 (.value(ha_1_sum));  // open: dp

  // Notes on the sheet:
  //   CARRY_OUT
  //   SUM
endmodule
