// Logisim project Exp.circ as structural Verilog: 9 circuits, main circuit main
module main (
  input  I0,
  input  I1,
  input  I2,
  input  I3,
  input  [1:0] S1,
  input  I4,
  input  I5,
  input  I6,
  input  I7,
  input  [1:0] S2,
  input  S3,
  output OUTPUT
);

  wire multiplexer_1_out, multiplexer_2_out;

  Multiplexer #(.select(2), .enable("false")) multiplexer_1 (
    .in0(I0), .in1(I1), .in2(I2), .in3(I3), .out(multiplexer_1_out), .sel(S1));
  Multiplexer #(.select(2), .enable("false")) multiplexer_2 (
    .in0(I4), .in1(I5), .in2(I6), .in3(I7), .out(multiplexer_2_out), .sel(S2));
  Multiplexer #(.enable("false")) multiplexer_3 (
    .in0(multiplexer_1_out), .in1(multiplexer_2_out), .out(OUTPUT), .sel(S3));
endmodule

// 2:1
module _2_1MUX (
  input  I0,
  input  I1,
  input  S0,
  output Output
);

  wire and_1_out, and_2_out, not_1_out;

  not not_1 (not_1_out, S0);
  and and_1 (and_1_out, not_1_out, I0);
  and and_2 (and_2_out, S0, I1);
  or or_1 (Output, and_1_out, and_2_out);
endmodule

// 4:1
module _4_1MUX (
  input  I0,
  input  I1,
  input  I2,
  input  I3,
  input  S0,
  input  S1,
  output Output
);

  wire and_1_out, and_2_out, and_3_out, and_4_out, not_1_out, not_2_out, not_3_out, not_4_out;

  not not_1 (not_1_out, S0);
  not not_2 (not_2_out, S1);
  not not_3 (not_3_out, S1);
  not not_4 (not_4_out, S0);
  and and_1 (and_1_out, not_1_out, not_2_out, I0);
  and and_2 (and_2_out, S0, not_3_out, I1);
  and and_3 (and_3_out, not_4_out, S1, I2);
  and and_4 (and_4_out, S0, S1, I3);
  or or_1 (Output, and_1_out, and_2_out, and_3_out, and_4_out);
endmodule

module _8_1_using_4_1_and_2_1 (
  input  I0,
  input  I1,
  input  I2,
  input  I3,
  input  I4,
  input  I5,
  input  I6,
  input  I7,
  input  S2,
  input  S1,
  input  S0,
  output Output
);

  wire n4_1mux_1_output, n4_1mux_2_output;

  _4_1MUX u_4_1mux_1 (.I0(I0), .I1(I1), .I2(I2), .I3(I3), .S0(S0), .S1(S1), .Output(n4_1mux_1_output));
  _4_1MUX u_4_1mux_2 (.I0(I4), .I1(I5), .I2(I6), .I3(I7), .S0(S0), .S1(S1), .Output(n4_1mux_2_output));
  _2_1MUX u_2_1mux_1 (.I0(n4_1mux_1_output), .I1(n4_1mux_2_output), .S0(S2), .Output(Output));
endmodule

// 1:4
module _1_4DeMUX (
  input  Y,
  input  S1,
  input  S0,
  output O0,
  output O1,
  output O2,
  output O3
);

  wire not_1_out, not_2_out, not_3_out, not_4_out;

  not not_1 (not_1_out, S1);
  not not_2 (not_2_out, S0);
  not not_3 (not_3_out, S1);
  not not_4 (not_4_out, S0);
  and and_1 (O3, S1, S0, Y);
  and and_2 (O0, not_1_out, not_2_out, Y);
  and and_3 (O1, not_3_out, S0, Y);
  and and_4 (O2, S1, not_4_out, Y);
endmodule

module _1_8_using_1_4 (
  input  Y,
  input  S2,
  input  S1,
  input  S0,
  output O0,
  output O1,
  output O2,
  output O3,
  output O4,
  output O5,
  output O6,
  output O7
);

  wire n1_4demux_1_o0, n1_4demux_1_o1, n1_4demux_1_o2;

  _1_4DeMUX u_1_4demux_1 (
    .Y(Y), .S1(n1_4demux_1_o2), .S0(S2), .O0(n1_4demux_1_o0), .O1(n1_4demux_1_o1), .O2(n1_4demux_1_o2),
    .O3(n1_4demux_1_o2));
  _1_4DeMUX u_1_4demux_2 (.Y(n1_4demux_1_o0), .S1(S1), .S0(S0), .O0(O0), .O1(O1), .O2(O2), .O3(O3));
  _1_4DeMUX u_1_4demux_3 (.Y(n1_4demux_1_o1), .S1(S1), .S0(S0), .O0(O4), .O1(O5), .O2(O6), .O3(O7));
  // also tied to GND on the sheet: n1_4demux_1_o2
endmodule

module _4_2Enc (
  input  I0,
  input  I1,
  input  I2,
  input  I3
);

  wire not_1_out, not_2_out, not_3_out, not_4_out, xor_1_out, xor_2_out, xor_3_out, xor_4_out;
  wire [1:0] or_1_out;

  not not_1 (not_1_out, I1);
  _7_Segment_Display u_7_segment_display_1 (
    .f(not_2_out), .a(not_2_out), .b(xor_1_out), .e(not_2_out), .d(not_2_out), .c(xor_1_out));  // open: g, dp
  not not_2 (not_2_out, I0);
  _7_Segment_Display u_7_segment_display_2 (
    .f(not_1_out), .a(not_1_out), .b(xor_2_out), .e(not_1_out), .d(not_1_out), .c(xor_2_out));  // open: g, dp
  _7_Segment_Display u_7_segment_display_3 (
    .f(not_3_out), .a(not_3_out), .b(xor_3_out), .e(not_3_out), .d(not_3_out), .c(xor_3_out));  // open: g, dp
  not not_3 (not_3_out, I2);
  _7_Segment_Display u_7_segment_display_4 (
    .f(not_4_out), .a(not_4_out), .b(xor_4_out), .e(not_4_out), .d(not_4_out), .c(xor_4_out));  // open: g, dp
  not not_4 (not_4_out, I3);
  xor xor_1 (xor_1_out, not_2_out, I0);
  xor xor_2 (xor_2_out, not_1_out, I1);
  xor xor_3 (xor_3_out, not_3_out, I2);
  xor xor_4 (xor_4_out, not_4_out, I3);
  or or_1 (or_1_out[0], I1, I3);
  or or_2 (or_1_out[1], I2, I3);
  Hex_Digit_Display hex_digit_display_1 (.value({2'b00, or_1_out}));  // open: dp
endmodule

// 2:4
module _2_4DeCoder (
  input  A0,
  input  A1,
  input  E,
  output O1,
  output O2,
  output O3,
  output O4
);

  wire not_1_out, not_2_out, not_3_out, not_4_out;

  not not_1 (not_1_out, A0);
  not not_2 (not_2_out, A1);
  not not_3 (not_3_out, A0);
  not not_4 (not_4_out, A1);
  and and_1 (O4, A0, A1, E);
  and and_2 (O1, not_1_out, not_2_out, E);
  and and_3 (O2, not_3_out, A1, E);
  and and_4 (O3, A0, not_4_out, E);
endmodule

module _3_8_using_2_4 (
  input  A0,
  input  A1,
  input  A2,
  output I0,
  output I1,
  output I2,
  output I3,
  output I4,
  output I5,
  output I6,
  output I7
);

  wire not_1_out;

  not not_1 (not_1_out, A2);
  _2_4DeCoder u_2_4decoder_1 (.A0(A0), .A1(A1), .E(not_1_out), .O1(I0), .O2(I1), .O3(I2), .O4(I3));
  _2_4DeCoder u_2_4decoder_2 (.A0(A0), .A1(A1), .E(A2), .O1(I4), .O2(I5), .O3(I6), .O4(I7));
endmodule
