// Logisim project Calender.circ as structural Verilog: 5 circuits, main circuit main
module main (
  input  M4,
  input  M3,
  input  M2,
  input  M1,
  input  L,
  output _28,
  output _29,
  output _30,
  output _31
);

  wire and_3_out, and_4_out, and_5_out, and_6_out, and_7_out, not_1_out, not_2_out, not_3_out, not_4_out,
       not_5_out, not_6_out, not_7_out, not_8_out, not_9_out, not_10_out, not_11_out, not_12_out, not_13_out,
       not_14_out, not_15_out;

  not not_1 (not_1_out, L);
  not not_2 (not_2_out, M1);
  not not_3 (not_3_out, M3);
  not not_4 (not_4_out, M4);
  not not_5 (not_5_out, M4);
  not not_6 (not_6_out, M3);
  not not_7 (not_7_out, M1);
  not not_8 (not_8_out, M4);
  not not_9 (not_9_out, M1);
  not not_10 (not_10_out, M3);
  not not_11 (not_11_out, M4);
  not not_12 (not_12_out, M3);
  not not_13 (not_13_out, M1);
  not not_14 (not_14_out, M2);
  not not_15 (not_15_out, M1);
  and and_1 (_28, not_1_out, not_2_out, M2, not_3_out, not_4_out);
  and and_2 (_29, not_5_out, not_6_out, M2, not_7_out, L);
  and and_3 (and_3_out, not_8_out, M3, not_9_out);
  and and_4 (and_4_out, M4, not_10_out, M1);
  and and_5 (and_5_out, not_11_out, M1);
  and and_6 (and_6_out, M4, not_12_out, not_13_out);
  and and_7 (and_7_out, M4, not_14_out, not_15_out);
  or or_1 (_30, and_3_out, and_4_out);
  or or_2 (_31, and_5_out, and_6_out, and_7_out);
endmodule

// Calendar
module Ex3 (
  input  M4,
  input  M3,
  input  M2,
  input  M1,
  input  L,
  output _28,
  output _29,
  output _30,
  output _31
);

  wire and_3_out, and_4_out, and_5_out, and_6_out, and_7_out, not_1_out, not_2_out, not_3_out, not_4_out,
       not_5_out, not_6_out, not_7_out, not_8_out, not_9_out, not_10_out, not_11_out, not_12_out, not_13_out,
       not_14_out, not_15_out;

  not not_1 (not_1_out, L);
  not not_2 (not_2_out, M1);
  not not_3 (not_3_out, M3);
  not not_4 (not_4_out, M4);
  not not_5 (not_5_out, M4);
  not not_6 (not_6_out, M3);
  not not_7 (not_7_out, M1);
  not not_8 (not_8_out, M4);
  not not_9 (not_9_out, M1);
  not not_10 (not_10_out, M3);
  not not_11 (not_11_out, M4);
  not not_12 (not_12_out, M3);
  not not_13 (not_13_out, M1);
  not not_14 (not_14_out, M2);
  not not_15 (not_15_out, M1);
  and and_1 (_28, not_1_out, not_2_out, M2, not_3_out, not_4_out);
  and and_2 (_29, not_5_out, not_6_out, M2, not_7_out, L);
  and and_3 (and_3_out, not_8_out, M3, not_9_out);
  and and_4 (and_4_out, M4, not_10_out, M1);
  and and_5 (and_5_out, not_11_out, M1);
  and and_6 (and_6_out, M4, not_12_out, not_13_out);
  and and_7 (and_7_out, M4, not_14_out, not_15_out);
  or or_1 (_30, and_3_out, and_4_out);
  or or_2 (_31, and_5_out, and_6_out, and_7_out);
endmodule

module Ex1 (
  input  Cin,
  input  [1:0] A_B,
  input  [2:0] A_B_Cin,
  output SUM,
  output SUM_2,
  output CARRY,
  output CARRY_2
);

  wire not_1_out;

  not not_1 (not_1_out, Cin);
  Multiplexer #(.select(2)) multiplexer_1 (
    .in0(Cin), .in1(not_1_out), .in2(not_1_out), .in3(Cin), .out(SUM), .sel(A_B));  // open: en
  Multiplexer #(.select(2)) multiplexer_2 (
    .in0(1'b0), .in1(Cin), .in2(Cin), .in3(1'b1), .out(CARRY), .sel(A_B));  // open: en
  Multiplexer #(.select(3)) multiplexer_3 (
    .in0(1'b0), .in1(1'b1), .in2(1'b1), .in3(1'b0), .in4(1'b1), .in5(1'b0), .in6(1'b0), .in7(1'b1),
    .out(SUM_2), .sel(A_B_Cin));  // open: en
  Multiplexer #(.select(3)) multiplexer_4 (
    .in0(1'b0), .in1(1'b0), .in2(1'b0), .in3(1'b1), .in4(1'b0), .in5(1'b1), .in6(1'b1), .in7(1'b1),
    .out(CARRY_2), .sel(A_B_Cin));  // open: en
endmodule

module Ex2 (
  input  in_1,
  input  in_2,
  input  in_3,
  input  in_4,
  input  in_5,
  input  in_6,
  input  in_7,
  input  in_8
);

  wire and_1_out, and_2_out, and_3_out, and_4_out, not_1_out, not_2_out, not_3_out, not_4_out, not_5_out,
       not_6_out, not_7_out, or_1_out, or_2_out, or_3_out;
  wire [2:0] priority_encoder_1_out;

  Priority_Encoder priority_encoder_1 (
    .in0(in_1), .in1(in_2), .in2(in_3), .in3(in_4), .in4(in_5), .in5(in_6), .in6(in_7), .in7(in_8),
    .out(priority_encoder_1_out));  // open: en_in, gs, en_out
  and and_1 (and_1_out, priority_encoder_1_out[1], not_1_out);
  not not_1 (not_1_out, priority_encoder_1_out[2]);
  not not_2 (not_2_out, priority_encoder_1_out[0]);
  not not_3 (not_3_out, priority_encoder_1_out[1]);
  and and_2 (and_2_out, not_3_out, not_4_out);
  not not_4 (not_4_out, priority_encoder_1_out[2]);
  not not_5 (not_5_out, priority_encoder_1_out[0]);
  and and_3 (and_3_out, not_5_out, priority_encoder_1_out[2]);
  not not_6 (not_6_out, priority_encoder_1_out[1]);
  not not_7 (not_7_out, priority_encoder_1_out[2]);
  or or_1 (or_1_out, priority_encoder_1_out[0], and_1_out);
  or or_2 (or_2_out, not_2_out, priority_encoder_1_out[1], priority_encoder_1_out[2]);
  or or_3 (or_3_out, and_2_out, and_3_out);
  and and_4 (and_4_out, priority_encoder_1_out[0], not_6_out, not_7_out);
  _7_Segment_Display u_7_segment_display_1 (
    .g(or_2_out), .f(1'b1), .a(1'b1), .b(or_1_out), .e(1'b1), .d(or_3_out), .c(and_4_out));  // open: dp
endmodule

module Ex3_display (
  input  L,
  input  [3:0] M4_M3_M2_M1
);

  wire ex3_1__28, ex3_1__29, ex3_1__30, ex3_1__31;

  Hex_Digit_Display hex_digit_display_1 (.value({3'b000, L}));  // open: dp
  _7_Segment_Display u_7_segment_display_1 (.b(ex3_1__31), .c(ex3_1__31));  // open: g, f, a, e, d, dp
  _7_Segment_Display u_7_segment_display_2 (
    .g(ex3_1__31), .a(ex3_1__31), .b(ex3_1__31), .d(ex3_1__31), .c(ex3_1__31));  // open: f, e, dp
  Hex_Digit_Display hex_digit_display_2 (.value(M4_M3_M2_M1));  // open: dp
  _7_Segment_Display u_7_segment_display_3 (
    .g(ex3_1__30), .a(ex3_1__30), .b(ex3_1__30), .d(ex3_1__30), .c(ex3_1__30));  // open: f, e, dp
  Ex3 ex3_1 (
    .M4(M4_M3_M2_M1[3]), .M3(M4_M3_M2_M1[2]), .M2(M4_M3_M2_M1[1]), .M1(M4_M3_M2_M1[0]), .L(L),
    ._28(ex3_1__28), ._29(ex3_1__29), ._30(ex3_1__30), ._31(ex3_1__31));
  _7_Segment_Display u_7_segment_display_4 (
    .g(ex3_1__29), .a(ex3_1__29), .b(ex3_1__29), .e(ex3_1__29), .d(ex3_1__29));  // open: f, c, dp
  _7_Segment_Display u_7_segment_display_5 (
    .f(ex3_1__30), .a(ex3_1__30), .b(ex3_1__30), .e(ex3_1__30), .d(ex3_1__30), .c(ex3_1__30));  // open: g, dp
  _7_Segment_Display u_7_segment_display_6 (
    .g(ex3_1__29), .f(ex3_1__29), .a(ex3_1__29), .b(ex3_1__29), .d(ex3_1__29), .c(ex3_1__29));  // open: e, dp
  _7_Segment_Display u_7_segment_display_7 (
    .g(ex3_1__28), .f(ex3_1__28), .a(ex3_1__28), .b(ex3_1__28), .e(ex3_1__28), .d(ex3_1__28), .c(ex3_1__28));  // open: dp
  _7_Segment_Display u_7_segment_display_8 (
    .g(ex3_1__28), .a(ex3_1__28), .b(ex3_1__28), .e(ex3_1__28), .d(ex3_1__28));  // open: f, c, dp

  // Notes on the sheet:
  //   LEAP
  //   31
  //   MONTH
  //   30
  //   29
  //   28
endmodule
