// Logisim project Ex1.circ as structural Verilog: 2 circuits, main circuit main
module main (
  input  Initial_Carry,
  input  in_2,
  input  in_3,
  input  [1:0] A_B,
  output Sum,
  output Carry
);

  wire not_1_out;

  not not_1 (not_1_out, Initial_Carry);
  Multiplexer #(.select(2)) multiplexer_1 (
    .in0(Initial_Carry), .in1(not_1_out), .in2(not_1_out), .in3(Initial_Carry), .out(Sum), .sel(A_B));  // open: en
  Multiplexer #(.select(2)) multiplexer_2 (
    .in0(in_2), .in1(Initial_Carry), .in2(Initial_Carry), .in3(in_3), .out(Carry), .sel(A_B));  // open: en
endmodule

module _8X1 (
  input  Initial_Carry,
  input  in_2,
  input  [2:0] A_B_C,
  output Carry,
  output Sum
);

  wire multiplexer_1_out, not_1_out, not_2_out;

  not not_1 (not_1_out, Initial_Carry);
  not not_2 (not_2_out, in_2);
  not not_3 (Carry, multiplexer_1_out);
  Multiplexer #(.select(3)) multiplexer_1 (
    .in0(in_2), .in1(not_1_out), .in2(not_1_out), .in3(not_2_out), .in4(not_1_out), .in5(not_2_out),
    .in6(not_2_out), .in7(Initial_Carry), .out(multiplexer_1_out), .sel(A_B_C));  // open: en
  Multiplexer #(.select(3)) multiplexer_2 (
    .in0(Initial_Carry), .in1(not_1_out), .in2(not_1_out), .in3(Initial_Carry), .in4(not_1_out),
    .in5(Initial_Carry), .in6(Initial_Carry), .in7(not_1_out), .out(Sum), .sel(A_B_C));  // open: en
endmodule
