// Logisim project Ex2.circ as structural Verilog: 1 circuit, main circuit main
module main (
  input  A3,
  input  A2,
  input  A1,
  input  A0
);

  wire and_1_out, and_2_out, and_3_out, and_4_out, not_1_out, not_2_out, not_3_out, not_4_out, not_5_out,
       not_6_out, or_1_out;

  not not_1 (not_1_out, A0);
  not not_2 (not_2_out, A3);
  not not_3 (not_3_out, A2);
  not not_4 (not_4_out, A2);
  not not_5 (not_5_out, A3);
  not not_6 (not_6_out, A1);
  and and_1 (and_1_out, not_2_out, not_3_out, A1);
  and and_2 (and_2_out, not_4_out, A1, A0);
  and and_3 (and_3_out, not_5_out, A2, A0);
  and and_4 (and_4_out, A2, not_6_out, A0);
  or or_1 (or_1_out, and_1_out, and_2_out, and_3_out, and_4_out);
  _7_Segment_Display u_7_segment_display_1 (
    .g(not_1_out), .f(not_1_out), .a(not_1_out), .e(not_1_out), .d(not_1_out));  // open: b, c, dp
  _7_Segment_Display u_7_segment_display_2 (.f(A0), .a(A0), .b(A0), .e(A0), .d(A0), .c(A0));  // open: g, dp
  _7_Segment_Display u_7_segment_display_3 (
    .g(or_1_out), .f(or_1_out), .a(or_1_out), .b(or_1_out), .e(or_1_out));  // open: d, c, dp
endmodule
