// Logisim project Ex3.circ as structural Verilog: 1 circuit, main circuit Month
module Month (
  input  M4,
  input  M3,
  input  M2,
  input  M1,
  input  L,
  output D28,
  output D29,
  output D30,
  output D31
);

  wire and_3_out, and_4_out, and_5_out, and_6_out, and_7_out, and_8_out, and_9_out, and_10_out, and_11_out,
       and_12_out, and_13_out, not_1_out, not_2_out, not_3_out, not_4_out, not_5_out, not_6_out, not_7_out,
       not_8_out, not_9_out, not_10_out, not_11_out, not_12_out, not_13_out, not_14_out, not_15_out,
       not_16_out, not_17_out, not_18_out, not_19_out, not_20_out, not_21_out, not_22_out, not_23_out,
       not_24_out, not_25_out, not_26_out, not_27_out, not_28_out, not_29_out, not_30_out, not_31_out,
       not_32_out;

  not not_1 (not_1_out, M4);
  not not_2 (not_2_out, M3);
  not not_3 (not_3_out, M2);
  not not_4 (not_4_out, L);
  not not_5 (not_5_out, M4);
  not not_6 (not_6_out, M3);
  not not_7 (not_7_out, M2);
  not not_8 (not_8_out, M4);
  not not_9 (not_9_out, M3);
  not not_10 (not_10_out, M4);
  not not_11 (not_11_out, M1);
  not not_12 (not_12_out, M3);
  not not_13 (not_13_out, M2);
  not not_14 (not_14_out, M1);
  not not_15 (not_15_out, M3);
  not not_16 (not_16_out, M1);
  not not_17 (not_17_out, M4);
  not not_18 (not_18_out, M3);
  not not_19 (not_19_out, M2);
  not not_20 (not_20_out, M1);
  not not_21 (not_21_out, M4);
  not not_22 (not_22_out, M3);
  not not_23 (not_23_out, M1);
  not not_24 (not_24_out, M4);
  not not_25 (not_25_out, M2);
  not not_26 (not_26_out, M1);
  not not_27 (not_27_out, M4);
  not not_28 (not_28_out, M2);
  not not_29 (not_29_out, M4);
  not not_30 (not_30_out, M3);
  not not_31 (not_31_out, M2);
  not not_32 (not_32_out, M3);
  and and_1 (D28, not_1_out, not_2_out, not_3_out, M1, not_4_out);
  and and_2 (D29, not_5_out, not_6_out, not_7_out, M1, L);
  and and_3 (and_3_out, not_8_out, not_9_out, M2, M1);
  and and_4 (and_4_out, not_10_out, M3, M2, not_11_out);
  and and_5 (and_5_out, M4, not_12_out, not_13_out, not_14_out);
  and and_6 (and_6_out, M4, not_15_out, M2, not_16_out);
  and and_7 (and_7_out, not_17_out, not_18_out, not_19_out, not_20_out);
  and and_8 (and_8_out, not_21_out, not_22_out, M2, not_23_out);
  and and_9 (and_9_out, not_24_out, M3, not_25_out, not_26_out);
  and and_10 (and_10_out, not_27_out, M3, not_28_out, M1);
  and and_11 (and_11_out, not_29_out, M3, M2, M1);
  and and_12 (and_12_out, M4, not_30_out, not_31_out, M1);
  and and_13 (and_13_out, M4, not_32_out, M2, M1);
  or or_1 (D30, and_3_out, and_4_out, and_5_out, and_6_out);
  or or_2 (D31, and_7_out, and_8_out, and_9_out, and_10_out, and_11_out, and_12_out, and_13_out);
endmodule
