// Logisim project Ex4.circ as structural Verilog: 1 circuit, main circuit main
module main (
  input  [3:0] Yo,
  input  [3:0] Y1,
  input  [3:0] Y2,
  input  [3:0] Y3
);

  wire and_1_out, and_2_out, nor_1_out, not_1_out, not_2_out, not_3_out, not_4_out, not_5_out, or_1_out,
       or_2_out, or_3_out;
  wire [0:0] and_3_out;

  Hex_Digit_Display hex_digit_display_1 (.value(Y3));  // open: dp
  Hex_Digit_Display hex_digit_display_2 (.value(Y1));  // open: dp
  Hex_Digit_Display hex_digit_display_3 (.value(Y2));  // open: dp
  Hex_Digit_Display hex_digit_display_4 (.value(Yo));  // open: dp
  nor nor_1 (nor_1_out, Yo[0], Yo[1], Yo[2], Yo[3], Y1[0], Y1[1], Y1[2], Y1[3]);
  not not_1 (not_1_out, Yo[0]);
  not not_2 (not_2_out, Yo[1]);
  not not_3 (not_3_out, Y1[0]);
  and and_1 (and_1_out, Y1[0], Yo[1], not_4_out);
  not not_4 (not_4_out, Yo[0]);
  and and_2 (and_2_out, not_1_out, not_2_out, not_3_out);
  or or_1 (or_1_out, and_2_out, and_1_out);
  or or_2 (or_2_out, or_1_out, nor_1_out);
  not not_5 (not_5_out, nor_1_out);
  or or_3 (or_3_out, or_1_out, not_5_out);
  and and_3 (and_3_out[0], or_2_out, or_3_out);
  Hex_Digit_Display hex_digit_display_5 (.value({3'b000, and_3_out[0]}));  // open: dp
endmodule
